# Fritzing sketch Schematics-arduino-rpi (saved by Fritzing 0.9.3b)
circuit board: 8.46667cm x 5.64444cm
breadboards: 1

parts:
  Componente1 = Arduino Uno (Rev3)
  R1 = Photocell (LDR) [package=THT]
  R2 = Resistor [tolerance=±5% resistance=330 package="0603 [SMD]"]
  R3 = Resistor [tolerance=±5% resistance=10k package="0603 [SMD]"]
  LED1 = LED - 5mm [color="Red (633nm)" package="5 mm [THT]"]

nets:
  N1: Componente1.A5/SCL, R1.pin_1, R3.Pin_0
  N2: Componente1.D10_PWM/SS, LED1.anode
  N3: Componente1.GND, R1.pin_0, R2.Pin_0
  N4: Componente1.5V, R3.Pin_1
  N5: R2.Pin_1, LED1.cathode

// code stored in the sketch: sketch_ldr.ino
/*
  Test Algorithm to control LED with a LDR temperature sensor.
*/
int ledPinBuiltin = LED_BUILTIN;
int ledPin = 10;
int ldrPin = A5;

void setup() {
  Serial.begin(115200);
  pinMode(ledPinBuiltin, OUTPUT);
  pinMode(ledPin, OUTPUT);
}

void loop() {

  int state = analogRead(ldrPin);
  Serial.print("Valor lido do LDR: ");
  Serial.println(state);

  int luminosity = map(state,0, 1023, 0, 255);
  Serial.print("Luminosidade: ");
  Serial.println(luminosity);
  Serial.println();

//  analogWrite(ledPin, luminosity);

  if (state > 800) {
    digitalWrite(ledPinBuiltin, HIGH);
  } else {
    digitalWrite(ledPinBuiltin, LOW);
  }
  delay(1000);
}
